// Logisim project LC-200-32.circ as structural Verilog: 6 circuits, main circuit Processor
module Processor (
  input  test_int_sig,
  output [31:0] diagnostic
);

  wire and_1_out, and_2_out, and_3_out, button_1_out, Clock, Clr, DrALU, DrIntEn, DrMEM, DrOFF, DrPC, DrReg,
       Int, IntAck, IntEn, LdA, LdB, LdIntEn, LdIR, LdMAR, LdPC, LdZ, multiplexer_2_out, multiplexer_3_out,
       multiplexer_4_out, multiplexer_6_out, multiplexer_7_out, not_1_out, not_2_out, register_1_q, undriven,
       undriven_2, WrMEM, WrREG, Z, ZeroDetectOut;
  wire [1:0] FUNC, RegSel;
  wire [3:0] IR_q, IR_q_3, IR_q_4, Opcode, Reg_num, rom_1_data;
  wire [23:0] mar_out;
  wire [31:0] A_q, B_q, Bus, multiplexer_5_out, PC, ram_1_data, registers_1_data_out, ZeroDetect;
  wire [31:4] IR_q_2;

  assign {Bus[31:3], Bus[4], Bus[1:0]} = DrPC ? PC : 32'bz;  // Controlled_Buffer controlled_buffer_1
  Register #(.width(1), .trigger("rising")) Z_Register (.D(ZeroDetectOut), .en(LdZ), .Q(Z), .clk(Clock), .clr(Clr));
  State_Machine state_machine_1 (
    .Clock(Clock), .OpCode(Opcode), .Z(Z), .Int(Int), .IntEn(IntEn), .Clr(Clr), .DrREG(DrReg), .DrMEM(DrMEM),
    .DrALU(DrALU), .DrPC(DrPC), .DrOFF(DrOFF), .LdPC(LdPC), .LdIR(LdIR), .LdMAR(LdMAR), .LdA(LdA), .LdB(LdB),
    .LdZ(LdZ), .WrREG(WrREG), .WrMEM(WrMEM), .RegSel(RegSel), .ALU_FUNC(FUNC), .LdIntEn(LdIntEn),
    .DrIntEn(DrIntEn), .IntAck(IntAck));
  Register #(.width(32), .trigger("rising")) A (
    .D({Bus[31:3], Bus[4], Bus[1:0]}), .en(LdA), .Q(A_q), .clk(Clock), .clr(Clr));
  ALU alu_1 (.FUNC(FUNC), .INPUT_A(A_q), .INPUT_B(B_q), .out_4(ZeroDetect));
  Register #(.width(32), .trigger("rising")) B (
    .D({Bus[31:3], Bus[4], Bus[1:0]}), .en(LdB), .Q(B_q), .clk(Clock), .clr(Clr));
  assign {Bus[31:3], Bus[4], Bus[1:0]} = DrALU ? ZeroDetect : 32'bz;  // Controlled_Buffer controlled_buffer_2
  Clock #(.highDuration(1), .lowDuration(1)) clock_1 (.out(Clock));
  Button button_1 (.out(button_1_out));
  Registers registers_1 (
    .WrReg(WrREG), .RegSel(Reg_num), .Data_In({Bus[31:3], Bus[4], Bus[1:0]}), .Clock(Clock),
    .ClearRegFile(Clr), .Data_Out(registers_1_data_out));
  assign {Bus[31:3], Bus[4], Bus[1:0]} = DrReg ? registers_1_data_out : 32'bz;  // Controlled_Buffer controlled_buffer_3
  Register #(.width(24), .trigger("rising")) MAR (
    .D({Bus[23:3], Bus[4], Bus[1:0]}), .en(LdMAR), .Q(mar_out), .clk(Clock), .clr(Clr));
  not not_1 (not_1_out, WrMEM);
  Device device_1 (
    .inta_in(IntAck), .\int (Int), .bus({Bus[31:3], Bus[4], Bus[1:0]}), .clr(Clr), .CLOCK(Clock));  // open: inta_out
  RAM #(.addrWidth(24), .dataWidth(32), .bus("separate")) ram_1 (
    .addr(mar_out), .din({Bus[31:3], Bus[4], Bus[1:0]}), .data(ram_1_data), .str(WrMEM), .clk(Clock),
    .ld(not_1_out), .clr(Clr));  // open: sel
  assign {Bus[31:3], Bus[4], Bus[1:0]} = DrMEM ? ram_1_data : 32'bz;  // Controlled_Buffer controlled_buffer_4
  Register #(.width(32), .trigger("rising")) IR (
    .D({Bus[31:3], Bus[4], Bus[1:0]}), .en(LdIR),
    .Q({Opcode, IR_q_4, IR_q_3, IR_q_2[31], IR_q_2[18:7], Bus[4], IR_q_2[5:4], IR_q}), .clk(Clock), .clr(Clr));
  Multiplexer #(.select(2), .width(4)) multiplexer_1 (
    .in0(IR_q_4), .in1(IR_q_3), .in2(IR_q), .in3(4'b1100), .out(Reg_num), .sel(RegSel));
  assign {Bus[31:3], Bus[4], Bus[1:0]} = DrOFF ? {{13{IR_q_2[31]}}, IR_q_2[18:7], Bus[4], IR_q_2[5:4], IR_q} : 32'bz;  // Controlled_Buffer controlled_buffer_5
  Comparator #(.width(32), .mode("unsigned")) comparator_1 (
    .a(ZeroDetect), .b({32{1'b0}}), .eq(ZeroDetectOut));  // open: gt, lt
  Multiplexer #(.select(1), .width(1)) multiplexer_2 (.in0(Bus[16]), .in1(1'b1), .out(multiplexer_2_out), .sel(Clr));
  Multiplexer #(.select(1), .width(1)) multiplexer_3 (.in0(LdIntEn), .in1(1'b1), .out(multiplexer_3_out), .sel(Clr));
  Multiplexer #(.select(1), .width(1)) multiplexer_4 (.in0(Clock), .in1(1'b1), .out(multiplexer_4_out), .sel(Clr));
  Multiplexer #(.select(1), .width(32)) multiplexer_5 (
    .in0({Bus[31:3], Bus[4], Bus[1:0]}), .in1(32'h10), .out(multiplexer_5_out), .sel(Clr));
  Button Reset (.out(Clr));
  assign IntEn = DrIntEn ? register_1_q : 1'bz;  // Controlled_Buffer controlled_buffer_6
  Register #(.width(1), .trigger("rising")) register_1 (
    .D(multiplexer_2_out), .en(multiplexer_3_out), .Q(register_1_q), .clk(multiplexer_4_out), .clr(undriven));
  Multiplexer #(.select(1), .width(1)) multiplexer_6 (.in0(LdPC), .in1(1'b1), .out(multiplexer_6_out), .sel(Clr));
  Multiplexer #(.select(1), .width(1)) multiplexer_7 (.in0(Clock), .in1(1'b1), .out(multiplexer_7_out), .sel(Clr));
  Register #(.width(32), .trigger("rising")) u_PC (
    .D(multiplexer_5_out), .en(multiplexer_6_out), .Q(PC), .clk(multiplexer_7_out), .clr(undriven_2));
  ROM #(.addrWidth(24), .dataWidth(4)) rom_1 (.addr(mar_out), .data(rom_1_data));  // open: sel
  and and_1 (and_1_out, WrMEM, rom_1_data[0]);
  Register #(.width(32), .trigger("rising")) hour (
    .D({Bus[31:3], Bus[4], Bus[1:0]}), .en(and_1_out), .clk(Clock));  // open: Q, clr
  and and_2 (and_2_out, WrMEM, rom_1_data[1]);
  not not_2 (not_2_out, WrREG);
  Register #(.width(32), .trigger("rising")) min (
    .D({Bus[31:3], Bus[4], Bus[1:0]}), .en(and_2_out), .clk(Clock));  // open: Q, clr
  RAM #(.addrWidth(4), .dataWidth(32), .bus("separate")) ram_2 (
    .addr(Reg_num), .din({Bus[31:3], Bus[4], Bus[1:0]}), .str(WrREG), .clk(Clock), .ld(not_2_out));  // open: data, sel, clr
  Register #(.width(32), .trigger("rising")) sec (
    .D({Bus[31:3], Bus[4], Bus[1:0]}), .en(and_3_out), .clk(Clock));  // open: Q, clr
  and and_3 (and_3_out, WrMEM, rom_1_data[2]);

  // Other names for the same wires on the sheet: Bus[2] = Bus[4]

  // Notes on the sheet:
  //   00 = RX
  //   01 = RY
  //   10 = RZ
  //   contents of rom_1 (hex, n*v repeats v):
  //   57*0 1 1 1 15728580*0 4 2 1
endmodule

module ALU (
  input  [31:0] INPUT_A,
  input  [31:0] INPUT_B,
  input  [1:0] FUNC,
  output [31:0] out_4
);

  wire [31:0] adder_1_out, adder_2_out, nand_1_out, subtractor_1_out;

  Adder #(.width(32)) adder_1 (.a(INPUT_A), .b(INPUT_B), .out(adder_1_out));  // open: cin, cout
  assign nand_1_out = ~(INPUT_A & INPUT_B);  // NAND_Gate nand_1, 32 bits wide
  Multiplexer #(.select(2), .width(32)) multiplexer_1 (
    .in0(adder_1_out), .in1(nand_1_out), .in2(subtractor_1_out), .in3(adder_2_out), .out(out_4), .sel(FUNC));
  Subtractor #(.width(32)) subtractor_1 (.a(INPUT_A), .b(INPUT_B), .out(subtractor_1_out));  // open: bin, bout
  Adder #(.width(32)) adder_2 (.a(INPUT_A), .b(32'h1), .out(adder_2_out));  // open: cin, cout
endmodule

module State_Machine (
  input  Clock,
  input  [3:0] OpCode,
  input  Z,
  input  Int,
  input  IntEn,
  input  Clr,
  output DrREG,
  output DrMEM,
  output DrALU,
  output DrPC,
  output DrOFF,
  output LdPC,
  output LdIR,
  output LdMAR,
  output LdA,
  output LdB,
  output LdZ,
  output WrREG,
  output WrMEM,
  output [1:0] RegSel,
  output [1:0] ALU_FUNC,
  output LdIntEn,
  output DrIntEn,
  output IntAck
);

  wire chkZ, OpTest;
  wire [0:0] and_1_out;
  wire [5:0] multiplexer_1_out, register_1_q, rom_1_data, rom_2_data, rom_3_data, rom_4_data;

  Register #(.width(6), .trigger("rising")) register_1 (
    .D(multiplexer_1_out), .en(Clock), .Q(register_1_q), .clk(Clock), .clr(Clr));
  Multiplexer #(.select(2), .width(6)) multiplexer_1 (
    .in0(rom_1_data), .in1(rom_2_data), .in2(rom_3_data), .in3(rom_4_data), .out(multiplexer_1_out),
    .sel({chkZ, OpTest}));
  ROM #(.addrWidth(6), .dataWidth(28)) rom_1 (
    .addr(register_1_q),
    .data({IntAck, DrIntEn, LdIntEn, chkZ, OpTest, ALU_FUNC, RegSel, WrMEM, WrREG, LdZ, LdB, LdA, LdMAR, LdIR, LdPC, DrOFF, DrPC, DrALU, DrMEM, DrREG, rom_1_data}));  // open: sel
  and and_1 (and_1_out[0], Int, IntEn);
  ROM #(.addrWidth(4), .dataWidth(6)) rom_2 (.addr(OpCode), .data(rom_2_data));  // open: sel
  ROM #(.addrWidth(2), .dataWidth(6)) rom_3 (.addr({1'b0, Z}), .data(rom_3_data));  // open: sel
  ROM #(.addrWidth(2), .dataWidth(6)) rom_4 (.addr({1'b0, and_1_out[0]}), .data(rom_4_data));  // open: sel

  // Notes on the sheet:
  //   contents of rom_1 (hex, n*v repeats v):
  //   5800002 6206 81a0203 e004 2400105 6086 1087 e00900 4049 8804a 120100 404c 840d a0100 404f 88050
  //   320100 a0212 840 4054 8415 2116 a0080 4058 8419 211a c0040 405c 8805d 41011e 1000000 4220 8421 900
  //   22 c064 2200100 4066 8067 2400100 180863 2400100 180863 2400100 180865
  //   contents of rom_2 (hex, n*v repeats v):
  //   8 e b 13 17 1b 11 22 0 0 23 25 28
  //   contents of rom_3 (hex, n*v repeats v):
  //   0 1f
  //   contents of rom_4 (hex, n*v repeats v):
  //   1 2
endmodule

module Zero_Detection (
  input  [31:0] In,
  output Out
);

  Comparator #(.width(32), .mode("unsigned")) comparator_1 (.a(In), .b({32{1'b0}}), .eq(Out));  // open: gt, lt
endmodule

module Registers (
  input  [31:0] Data_In,
  input  WrReg,
  input  [3:0] RegSel,
  input  Clock,
  input  ClearRegFile,
  output [31:0] Data_Out
);

  wire and_1_out, and_2_out, and_3_out, and_4_out, and_5_out, and_6_out, and_7_out, and_8_out, and_9_out,
       and_10_out, and_11_out, and_12_out, and_13_out, and_14_out, and_15_out, and_16_out, decoder_1_out0,
       decoder_1_out1, decoder_1_out2, decoder_1_out3, decoder_1_out4, decoder_1_out5, decoder_1_out6,
       decoder_1_out7, decoder_1_out8, decoder_1_out9, decoder_1_out10, decoder_1_out11, decoder_1_out12,
       decoder_1_out13, decoder_1_out14, decoder_1_out15;
  wire [31:0] a0, a1, a2, at, k0, pr, ra, s0, s1, s2, sp, t0, t1, t2, v0, zero;

  Decoder #(.select(4), .tristate("false")) decoder_1 (
    .out0(decoder_1_out0), .out1(decoder_1_out1), .out2(decoder_1_out2), .out3(decoder_1_out3),
    .out4(decoder_1_out4), .out5(decoder_1_out5), .out6(decoder_1_out6), .out7(decoder_1_out7),
    .out8(decoder_1_out8), .out9(decoder_1_out9), .out10(decoder_1_out10), .out11(decoder_1_out11),
    .out12(decoder_1_out12), .out13(decoder_1_out13), .out14(decoder_1_out14), .out15(decoder_1_out15),
    .sel(RegSel));
  and and_1 (and_1_out, decoder_1_out0, WrReg);
  and and_2 (and_2_out, decoder_1_out1, WrReg);
  and and_3 (and_3_out, decoder_1_out2, WrReg);
  and and_4 (and_4_out, decoder_1_out3, WrReg);
  and and_5 (and_5_out, decoder_1_out4, WrReg);
  and and_6 (and_6_out, decoder_1_out5, WrReg);
  and and_7 (and_7_out, decoder_1_out6, WrReg);
  and and_8 (and_8_out, decoder_1_out7, WrReg);
  and and_9 (and_9_out, decoder_1_out8, WrReg);
  and and_10 (and_10_out, decoder_1_out9, WrReg);
  and and_11 (and_11_out, decoder_1_out10, WrReg);
  and and_12 (and_12_out, decoder_1_out11, WrReg);
  and and_13 (and_13_out, decoder_1_out12, WrReg);
  and and_14 (and_14_out, decoder_1_out13, WrReg);
  and and_15 (and_15_out, decoder_1_out14, WrReg);
  and and_16 (and_16_out, decoder_1_out15, WrReg);
  Register #(.width(32), .trigger("rising")) u_zero (.D(Data_In), .en(and_1_out), .Q(zero), .clk(Clock), .clr(1'b1));
  Register #(.width(32), .trigger("rising")) u_at (
    .D(Data_In), .en(and_2_out), .Q(at), .clk(Clock), .clr(ClearRegFile));
  Register #(.width(32), .trigger("rising")) u_v0 (
    .D(Data_In), .en(and_3_out), .Q(v0), .clk(Clock), .clr(ClearRegFile));
  Register #(.width(32), .trigger("rising")) u_a0 (
    .D(Data_In), .en(and_4_out), .Q(a0), .clk(Clock), .clr(ClearRegFile));
  Register #(.width(32), .trigger("rising")) u_a1 (
    .D(Data_In), .en(and_5_out), .Q(a1), .clk(Clock), .clr(ClearRegFile));
  Register #(.width(32), .trigger("rising")) u_a2 (
    .D(Data_In), .en(and_6_out), .Q(a2), .clk(Clock), .clr(ClearRegFile));
  Register #(.width(32), .trigger("rising")) u_t0 (
    .D(Data_In), .en(and_7_out), .Q(t0), .clk(Clock), .clr(ClearRegFile));
  Register #(.width(32), .trigger("rising")) u_t1 (
    .D(Data_In), .en(and_8_out), .Q(t1), .clk(Clock), .clr(ClearRegFile));
  Register #(.width(32), .trigger("rising")) u_t2 (
    .D(Data_In), .en(and_9_out), .Q(t2), .clk(Clock), .clr(ClearRegFile));
  Register #(.width(32), .trigger("rising")) u_s0 (
    .D(Data_In), .en(and_10_out), .Q(s0), .clk(Clock), .clr(ClearRegFile));
  Register #(.width(32), .trigger("rising")) u_s1 (
    .D(Data_In), .en(and_11_out), .Q(s1), .clk(Clock), .clr(ClearRegFile));
  Register #(.width(32), .trigger("rising")) u_s2 (
    .D(Data_In), .en(and_12_out), .Q(s2), .clk(Clock), .clr(ClearRegFile));
  Register #(.width(32), .trigger("rising")) u_k0 (
    .D(Data_In), .en(and_13_out), .Q(k0), .clk(Clock), .clr(ClearRegFile));
  Register #(.width(32), .trigger("rising")) u_sp (
    .D(Data_In), .en(and_14_out), .Q(sp), .clk(Clock), .clr(ClearRegFile));
  Register #(.width(32), .trigger("rising")) u_pr (
    .D(Data_In), .en(and_15_out), .Q(pr), .clk(Clock), .clr(ClearRegFile));
  Register #(.width(32), .trigger("rising")) u_ra (
    .D(Data_In), .en(and_16_out), .Q(ra), .clk(Clock), .clr(ClearRegFile));
  Multiplexer #(.select(4), .width(32)) multiplexer_1 (
    .in0(zero), .in1(at), .in2(v0), .in3(a0), .in4(a1), .in5(a2), .in6(t0), .in7(t1), .in8(t2), .in9(s0),
    .in10(s1), .in11(s2), .in12(k0), .in13(sp), .in14(pr), .in15(ra), .out(Data_Out), .sel(RegSel));

  // Other names for the same wires on the sheet: Din[31:0] = Data_In; en = WrReg
endmodule

module Interrupt_Interface_2 (
  input  inta_in,
  input  int_in,
  input  [31:0] device_id,
  input  CLOCK,
  output int_out,
  output inta_out,
  output [31:0] bus
);

  wire ack_signal, multiplexer_1_out, not_1_out, register_1_q;

  Multiplexer #(.select(2), .width(1)) multiplexer_1 (
    .in0(int_in), .in3(1'b0), .out(multiplexer_1_out), .sel({inta_in, int_out}));  // open: in1, in2
  Register #(.width(1), .trigger("rising")) int_register (
    .D(multiplexer_1_out), .Q(int_out), .clk(CLOCK));  // open: en, clr
  and and_1 (ack_signal, int_out, inta_in);
  not not_1 (not_1_out, int_out);
  and and_2 (inta_out, not_1_out, inta_in);
  assign bus = register_1_q ? device_id : 32'bz;  // Controlled_Buffer controlled_buffer_1
  Register #(.width(1), .trigger("rising")) register_1 (
    .D(ack_signal), .Q(register_1_q), .clk(CLOCK));  // open: en, clr
  Register #(.width(1), .trigger("rising")) register_2 ();  // open: D, en, Q, clk, clr
endmodule
