// Logisim project intergenerator.circ as structural Verilog: 3 circuits, main circuit main
module main (
  input  CLK,
  output IntOut
);

  wire [9:0] adder_1_out, register_1_q;

  Adder #(.width(10)) adder_1 (.a(10'h1), .b(register_1_q), .out(adder_1_out));  // open: cin, cout
  Register #(.width(10), .trigger("rising")) register_1 (
    .D(adder_1_out), .en(1'b1), .Q(register_1_q), .clk(CLK));  // open: clr
  Comparator #(.width(10), .mode("unsigned")) comparator_1 (
    .a({10{1'b1}}), .b(register_1_q), .eq(IntOut));  // open: gt, lt
endmodule

module Interrupt_Interface (
  input  inta_in,
  input  clr,
  input  int_in,
  input  [31:0] device_id,
  input  CLOCK,
  output int_out,
  output inta_out,
  output [31:0] bus
);

  wire ack_signal, multiplexer_1_out, not_1_out, register_2_q;

  Register #(.width(1), .trigger("rising")) register_1 ();  // open: D, en, Q, clk, clr
  Multiplexer #(.select(2), .width(1)) multiplexer_1 (
    .in0(int_in), .in3(1'b0), .out(multiplexer_1_out), .sel({inta_in, int_out}));  // open: in1, in2
  Register #(.width(1), .trigger("rising")) int_register (
    .D(multiplexer_1_out), .Q(int_out), .clk(CLOCK), .clr(clr));  // open: en
  and and_1 (ack_signal, int_out, inta_in);
  not not_1 (not_1_out, int_out);
  and and_2 (inta_out, not_1_out, inta_in);
  assign bus = register_2_q ? device_id : 32'bz;  // Controlled_Buffer controlled_buffer_1
  Register #(.width(1), .trigger("rising")) register_2 (
    .D(ack_signal), .Q(register_2_q), .clk(CLOCK));  // open: en, clr
endmodule

module Device (
  input  inta_in,
  input  CLOCK,
  input  clr,
  output \int ,
  output [31:0] bus,
  output inta_out
);

  wire main_1_intout;

  Interrupt_Interface interrupt_interface_1 (
    .inta_in(inta_in), .clr(clr), .int_out(\int ), .bus(bus), .int_in(main_1_intout), .device_id(32'h1),
    .inta_out(inta_out), .CLOCK(CLOCK));
  main main_1 (.IntOut(main_1_intout), .CLK(CLOCK));
endmodule
